# Fritzing sketch iVento-diagram (saved by Fritzing 0.9.3b)
breadboards: 1

parts:
  Part1 = Arduino Uno (Rev3)
  LCD1 = LCD screen
  R1 = Rotary Potentiometer (Small) [maximum_resistance=100kΩ package=THT]
  U2 = ESP8266 WiFi Module [part_number=ESP8266]
  RHT1 = Humidity and Temperature Sensor RHT03
  Relay_5V1 = Keyes Relay [package=THT]

nets:
  N1: Part1.D8, LCD1.DB4
  N2: Part1.D9_PWM, LCD1.DB5
  N3: Part1.D10_PWM/SS, LCD1.DB6
  N4: Part1.D11_PWM/MOSI, LCD1.DB7
  N5: Part1.D2, RHT1.Data-signal
  N6: Part1.D3_PWM, Relay_5V1.power
  N7: Part1.D4, LCD1.RS
  N8: Part1.D5_PWM, LCD1.E
  N9: Part1.D6_PWM, U2.TXD
  N10: Part1.D7, U2.RXD
  3V3: Part1.3V3, U2.VCC, U2.CH_PD
  5V: Part1.5V, LCD1.VDD, RHT1.Vcc, Relay_5V1.signal
  GND: Part1.GND, LCD1.VSS, LCD1.R/W, U2.GND, RHT1.GND_2, Relay_5V1.ground
  N11: LCD1.V0, R1.wiper

custom parts:
  ESP8266 WiFi Module: Generic WiFi Module based on the ESP8266 with onboard PCB antenna and UART communications
  Keyes Relay: The Keyes 5V relay module is suitable for SCM development, home appliance control. It uses a 5V~12V TIL control signal which can control DC / AC signal.
